# Fritzing sketch 555 (saved by Fritzing 0.9.3b)
breadboards: 1

parts:
  U1 = 555 Timer [package="DIP8 [THT]"]
  U2 = 555 Timer [package="DIP8 [THT]"]
  J1 = Piezo Speaker
  C1 = Ceramic Capacitor [capacitance=100nF package="100 mil [THT, multilayer]"]
  R1 = Resistor [tolerance=±5% resistance=1k package=THT]

nets:
  N1: U1.Output, R1.Pin_0
  5V: U1.Reset, U1.Vcc_Supply_Voltage
  GND: U2.Ground, J1.pin2
  N2: U2.Output, C1.0
  N3: U2.Control_Voltage, R1.Pin_1
